# Fritzing sketch bluetooth_robot_circuit (saved by Fritzing 0.9.3b)
breadboards: 1

parts:
  M1 = DC Motor
  M2 = DC Motor
  IC1 = L293D [package=THT]
  VCC1 = Battery block 9V
  Part1 = Arduino Uno (Rev3)
  Part2 = Bluetooth HC-05 Macho

nets:
  N1: M1.pin_1, IC1.Out_4_(_Controlled_by_Enable_2_)
  N2: M1.pin_2, IC1.Out_3_(_Controlled_by_Enable_2_)
  N3: M2.pin_1, IC1.Out_2_(_Controlled_by_Enable_1_)
  N4: M2.pin_2, IC1.Out_1_(_Controlled_by_Enable_1_)
  5V: IC1.Enable_1, IC1.Enable_2, IC1.+V, Part1.5V, Part2.VCC
  N5: IC1.In_1, Part1.D8
  GND: IC1.0V, VCC1.-, Part1.GND, Part2.GND
  N6: IC1.In_2, Part1.D9_PWM
  N7: IC1.+Vmotor, VCC1.+, Part1.VIN
  N8: IC1.In_3, Part1.D6_PWM
  N9: IC1.In_4, Part1.D7
  N10: Part1.D0/RX, Part2.TXD
  N11: Part1.D1/TX, Part2.RXD
